# Fritzing sketch Circiut.Design_Fritzing (saved by Fritzing 0.8.7b)

parts:
  Eleman1 = Arduino Nano (Rev3.0)
  BT1 = Bluetooth HC-06d [package=THT]
  SP1 = SPEAKER [package=pcb_mount_speaker]
  Eleman2 = MicroSD Card Module

nets:
  N1: Eleman1.D1/TX, BT1.RXD
  N2: Eleman1.D0/RX, BT1.TXD
  GND: Eleman1.GND, BT1.GND, SP1.+, Eleman2.GND
  N3: Eleman1.D4, Eleman2.CS
  N4: Eleman1.D9, SP1.-
  N5: Eleman1.D11/MOSI, Eleman2.MOSI
  N6: Eleman1.D12/MISO, Eleman2.MISO
  VCC: Eleman1.5V, BT1.VCC, Eleman2.VCC
  N7: Eleman1.D13/SCK, Eleman2.SCK

notes:
  Sırası ile
  -GND
  -VCC
  -MISO (D12)
  -MOSI (D11)
  -SCK (D13^)
  -CS(D4)

custom parts:
  Bluetooth HC-06d: Bluetooth HC-06 - face down, pins down 16.5mm x 37.5mm PCB
